// Logisim project Computador Simulado.circ as structural Verilog: 8 circuits, main circuit Computador
module Computador (
);

  wire CLOCK, clock_1_out, cpu_1_p2, cpu_1_p6, cpu_1_p7, cpu_1_p8, cpu_1_p9, cpu_1_p13, cpu_1_p14, cpu_1_p15,
       not_1_out;
  wire [1:0] cpu_1_p11;
  wire [4:0] cpu_1_p10;
  wire [7:0] cpu_1_p3, cpu_1_p4, cpu_1_p5;

  Clock clock_1 (.out(clock_1_out));
  assign CLOCK = not_1_out ? clock_1_out : 1'bz;  // Controlled_Buffer controlled_buffer_1
  not not_1 (not_1_out, cpu_1_p7);
  // CPU cpu_1: pin names not known; wires that end beside it: CLOCK, cpu_1_p2, cpu_1_p3, cpu_1_p4, cpu_1_p5, cpu_1_p6, cpu_1_p7, cpu_1_p8, cpu_1_p9, cpu_1_p10, cpu_1_p11, cpu_1_p6, cpu_1_p13, cpu_1_p14, cpu_1_p15
  ROM #(.addrWidth(5)) rom_1 (.addr(cpu_1_p10), .data(cpu_1_p3));  // open: sel
  RAM #(.addrWidth(2), .bus("separate")) ram_1 (
    .addr(cpu_1_p11), .din(cpu_1_p5), .data(cpu_1_p4), .str(cpu_1_p15), .clk(CLOCK), .ld(cpu_1_p14));  // open: sel, clr

  // Notes on the sheet:
  //   Barramento de Endereços
  //   Barramento de Controle
  //   Barramento de Dados
  //   MEMÓRIA DE PROGRAMA
  //   MEMÓRIA DE DADOS
  //   contents of rom_1 (hex, n*v repeats v):
  //   d0 d5 da 86 cc 93 c0 ec a0
endmodule

module CPU (
  input  CLOCK,
  input  [7:0] Dado_ROM,
  input  [7:0] Dado_RAM,
  output [4:0] out_4,
  output HLT,
  output RDM,
  output STR,
  output [7:0] OUT_RAM,
  output [4:0] End_ROM,
  output [1:0] End_RAM
);

  wire ADD, DIV, MOV_X__Ra, MOV_X__Y, MUL, SUB;
  wire [1:0] End_1, End_2;
  wire [3:0] OPCODE;
  wire [7:0] ALU_OUT, RX, RY;

  Contador_do_Programa contador_do_programa_1 (.Clock(CLOCK), .HLT(HLT), .END_ROM(out_4));
  \Registrador_de_Instrução  \registrador_de_instrução_1  (.Dado_UC(Dado_ROM), .Clock(CLOCK));  // open: Instrução
  Banco_de_Registradores banco_de_registradores_1 (
    .ALU_OUT(ALU_OUT), .Dado_RAM(Dado_RAM), .RDM(RDM), .RX(End_1), .STR(STR), .RY(End_2), .HLT(HLT),
    .MOV_X_Y(MOV_X__Y), .MUL(MUL), .SUB(SUB), .Clock(CLOCK), .DIV(DIV), .OUT_RAM(OUT_RAM),
    .MOV_Ra(MOV_X__Ra), .ALU_Y(RY), .ALU_X(RX), .ADD(ADD));
  Unidade_de_Controle unidade_de_controle_1 (
    .Dado_ROM(Dado_ROM), .Contador(out_4), .Clock(CLOCK), .End_2(End_2), .DIV(DIV), .SUB(SUB),
    .End__1(End_1), .MUL(MUL), .ADD(ADD), .Operador(OPCODE), .HLT(HLT), .MOV_Rx___Ry(MOV_X__Y),
    .MOV_Rx___Ra(MOV_X__Ra), .RDM_Rx___End(RDM), .STR_End___Rx(STR), .End_ROM(End_ROM), .End__RAM(End_RAM));
  ALU alu_1 (.RX(RX), .RY(RY), .OPCODE(OPCODE), .Resultado(ALU_OUT));

  // Other names for the same wires on the sheet: Contador[4:0] = out_4

  // Notes on the sheet:
  //   CPU
endmodule

// PC
module Contador_do_Programa (
  input  Clock,
  input  HLT,
  output [4:0] END_ROM
);

  Counter #(.width(5), .max('h1f)) Contador_do_programa (
    .Q(END_ROM), .clk(Clock), .clr(HLT));  // open: load, D, count, carry
endmodule

// IR
module \Registrador_de_Instrução  (
  input  [7:0] Dado_UC,
  input  Clock,
  output [7:0] \Instrução 
);

  Register Resgistrador_De_Instr (.D(Dado_UC), .Q(\Instrução ), .clk(Clock));  // open: en, clr
endmodule

module Unidade_de_Controle (
  input  [7:0] Dado_ROM,
  input  [4:0] Contador,
  input  Clock,
  output [1:0] End_2,
  output DIV,
  output SUB,
  output [1:0] End__1,
  output MUL,
  output ADD,
  output [3:0] Operador,
  output HLT,
  output MOV_Rx___Ry,
  output MOV_Rx___Ra,
  output RDM_Rx___End,
  output STR_End___Rx,
  output [4:0] End_ROM,
  output [1:0] End__RAM
);

  Decoder #(.select(4)) decoder_1 (
    .out6(DIV), .out7(SUB), .out8(MUL), .out9(ADD), .out10(HLT), .out11(MOV_Rx___Ry), .out12(MOV_Rx___Ra),
    .out13(RDM_Rx___End), .out14(STR_End___Rx), .sel(Dado_ROM[7:4]));  // open: out0, out1, out2, out3, out4, out5, out15, en
  Unidade_de_Busca unidade_de_busca_1 (
    .Contador(Contador), .Clock(Clock), .RDM_Rx___End(RDM_Rx___End), .End_2(Dado_ROM[1:0]),
    .End__1(Dado_ROM[3:2]), .STR_End___Rx(STR_End___Rx), .End_Instr(End_ROM), .End_RAM(End__RAM));

  assign End_2 = Dado_ROM[1:0];
  assign End__1 = Dado_ROM[3:2];
  assign Operador = Dado_ROM[7:4];

  // Other names for the same wires on the sheet: End_1[1:0] = Dado_ROM[3:2]; RDM = RDM_Rx___End; STR = STR_End___Rx

  // Notes on the sheet:
  //   Unidade de Controle
endmodule

module Unidade_de_Busca (
  input  [4:0] Contador,
  input  Clock,
  input  RDM_Rx___End,
  input  [1:0] End_2,
  input  [1:0] End__1,
  input  STR_End___Rx,
  output [4:0] End_Instr,
  output [1:0] End_RAM
);

  assign End_RAM = RDM_Rx___End ? End_2 : 2'bz;  // Controlled_Buffer controlled_buffer_1
  assign End_RAM = STR_End___Rx ? End__1 : 2'bz;  // Controlled_Buffer controlled_buffer_2
  Register #(.width(5)) register_1 (.D(Contador), .Q(End_Instr), .clk(Clock));  // open: en, clr

  // Notes on the sheet:
  //   Unidade de Busca
endmodule

// B. Reg
module Banco_de_Registradores (
  input  [7:0] Dado_RAM,
  input  MOV_Ra,
  input  [7:0] ALU_OUT,
  input  RDM,
  input  Clock,
  input  STR,
  input  [1:0] RX,
  input  HLT,
  input  [1:0] RY,
  input  MUL,
  input  SUB,
  input  DIV,
  input  ADD,
  input  MOV_X_Y,
  output [7:0] OUT_RAM,
  output [7:0] ALU_X,
  output [7:0] ALU_Y
);

  wire not_1_out, OP;
  wire [1:0] RX_t;
  wire [7:0] controlled_buffer_4_out, controlled_buffer_6_out, DRAM, multiplexer_1_out, multiplexer_2_out,
       R0_IN, R0_q, R1_IN, R1_q, R2_IN, R2_q, R3_IN, R3_q, Ra, RA_q;

  assign DRAM = RDM ? Dado_RAM : 8'bz;  // Controlled_Buffer controlled_buffer_1
  assign RX_t = not_1_out ? RX : 2'bz;  // Controlled_Buffer controlled_buffer_2
  assign RX_t = STR ? RY : 2'bz;  // Controlled_Buffer controlled_buffer_3
  not not_1 (not_1_out, STR);
  or or_1 (OP, MUL, SUB, DIV, ADD);
  assign controlled_buffer_4_out = OP ? ALU_OUT : 8'bz;  // Controlled_Buffer controlled_buffer_4
  Register u_RA (.D(controlled_buffer_4_out), .Q(RA_q), .clk(Clock), .clr(HLT));  // open: en
  Register R0 (.D(R0_IN), .Q(R0_q), .clk(Clock), .clr(HLT));  // open: en
  Register R1 (.D(R1_IN), .Q(R1_q), .clk(Clock), .clr(HLT));  // open: en
  Register R2 (.D(R2_IN), .Q(R2_q), .clk(Clock), .clr(HLT));  // open: en
  Register R3 (.D(R3_IN), .Q(R3_q), .clk(Clock), .clr(HLT));  // open: en
  assign Ra = MOV_Ra ? RA_q : 8'bz;  // Controlled_Buffer controlled_buffer_5
  Demultiplexer #(.select(2), .width(8), .tristate("true")) demultiplexer_1 (
    .out0(R0_IN), .out1(R1_IN), .out2(R2_IN), .out3(R3_IN), .in(controlled_buffer_6_out), .sel(RX_t));  // open: en
  assign controlled_buffer_6_out = MOV_X_Y ? multiplexer_2_out : 8'bz;  // Controlled_Buffer controlled_buffer_6
  Demultiplexer #(.select(2), .width(8), .tristate("true")) demultiplexer_2 (
    .out0(R0_IN), .out1(R1_IN), .out2(R2_IN), .out3(R3_IN), .in(DRAM), .sel(RX_t));  // open: en
  Demultiplexer #(.select(2), .width(8), .tristate("true")) demultiplexer_3 (
    .out0(R0_IN), .out1(R1_IN), .out2(R2_IN), .out3(R3_IN), .in(Ra), .sel(RX_t));  // open: en
  assign OUT_RAM = STR ? multiplexer_1_out : 8'bz;  // Controlled_Buffer controlled_buffer_7
  Multiplexer #(.select(2), .width(8)) multiplexer_1 (
    .in0(R0_q), .in1(R1_q), .in2(R2_q), .in3(R3_q), .out(multiplexer_1_out), .sel(RX_t));  // open: en
  Multiplexer #(.select(2), .width(8)) multiplexer_2 (
    .in0(R0_q), .in1(R1_q), .in2(R2_q), .in3(R3_q), .out(multiplexer_2_out), .sel(RY));  // open: en
  assign ALU_X = OP ? multiplexer_1_out : 8'bz;  // Controlled_Buffer controlled_buffer_8
  assign ALU_Y = OP ? multiplexer_2_out : 8'bz;  // Controlled_Buffer controlled_buffer_9

  // Notes on the sheet:
  //   Banco de Registradores
endmodule

module ALU (
  input  [7:0] RX,
  input  [7:0] RY,
  input  [3:0] OPCODE,
  output [7:0] Resultado
);

  wire [7:0] adder_1_out, divider_1_out, multiplier_1_out, subtractor_1_out;

  Divider divider_1 (.a(RX), .b(RY), .out(divider_1_out));  // open: upper, rem
  Subtractor subtractor_1 (.a(RX), .b(RY), .out(subtractor_1_out));  // open: bin, bout
  Multiplier multiplier_1 (.a(RX), .b(RY), .out(multiplier_1_out));  // open: cin, cout
  Adder adder_1 (.a(RX), .b(RY), .out(adder_1_out));  // open: cin, cout
  Multiplexer #(.select(4), .width(8)) multiplexer_1 (
    .in6(divider_1_out), .in7(subtractor_1_out), .in8(multiplier_1_out), .in9(adder_1_out), .out(Resultado),
    .sel(OPCODE));  // open: in0, in1, in2, in3, in4, in5, in10, in11, in12, in13, in14, in15, en
endmodule
